// Logisim project Lab3.circ as structural Verilog
module Control (
  input  I30,
  input  I14,
  input  I13,
  input  I12,
  input  I6,
  input  I5,
  input  I4,
  output ALU_CTRL3,
  output ALU_CTRL2,
  output ALU_CTRL1,
  output ALU_CTRL0,
  output ALU_Src
);

  wire and_2_out, not_1_out, not_2_out, not_3_out, not_4_out, not_5_out;

  not not_1 (not_1_out, I14);
  not not_2 (not_2_out, I13);
  not not_3 (not_3_out, I12);
  not not_4 (not_4_out, I5);
  not not_5 (not_5_out, I4);
  and and_1 (ALU_CTRL2, I30, not_2_out, I5);
  or or_1 (ALU_CTRL1, not_2_out, not_5_out);
  and and_2 (and_2_out, I13, not_3_out);
  or or_2 (ALU_Src, not_4_out, not_5_out);
  or or_3 (ALU_CTRL0, not_1_out, and_2_out);

  assign ALU_CTRL3 = 1'b0;
endmodule

module add (
  input  A,
  input  B,
  input  C_in,
  output S,
  output C_out
);

  wire and_1_out, and_2_out, xor_1_out;

  xor xor_1 (xor_1_out, A, B);
  xor xor_2 (S, xor_1_out, C_in);
  and and_1 (and_1_out, xor_1_out, C_in);
  and and_2 (and_2_out, A, B);
  or or_1 (C_out, and_1_out, and_2_out);
endmodule

module One_bit_ALU (
  input  [3:0] ALU_Ctrl,
  input  A,
  input  B,
  input  C_in,
  output R,
  output C_out
);

  wire add_1_s, and_1_out, multiplexer_1_out, not_1_out, or_1_out, xor_1_out;

  Multiplexer #(.enable("false")) multiplexer_1 (.in0(B), .in1(not_1_out), .out(multiplexer_1_out), .sel(ALU_Ctrl[2]));
  not not_1 (not_1_out, B);
  and and_1 (and_1_out, A, multiplexer_1_out);
  or or_1 (or_1_out, A, multiplexer_1_out);
  xor xor_1 (xor_1_out, A, multiplexer_1_out);
  Multiplexer #(.enable("false"), .select(2)) multiplexer_2 (
    .in0(and_1_out), .in1(or_1_out), .in2(xor_1_out), .in3(add_1_s), .out(R), .sel(ALU_Ctrl[1:0]));
  add add_1 (.A(A), .B(multiplexer_1_out), .C_in(C_in), .S(add_1_s), .C_out(C_out));
endmodule

module ALU4 (
  input  [3:0] ALU_Ctrl,
  input  [3:0] A,
  input  [3:0] B,
  input  C_in,
  output [3:0] R,
  output C_out
);

  wire one_bit_alu_1_c_out, one_bit_alu_2_c_out, one_bit_alu_3_c_out;

  One_bit_ALU one_bit_alu_1 (
    .ALU_Ctrl(ALU_Ctrl), .A(A[0]), .B(B[0]), .C_in(C_in), .R(R[0]), .C_out(one_bit_alu_1_c_out));
  One_bit_ALU one_bit_alu_2 (
    .ALU_Ctrl(ALU_Ctrl), .A(A[1]), .B(B[1]), .C_in(one_bit_alu_1_c_out), .R(R[1]), .C_out(one_bit_alu_2_c_out));
  One_bit_ALU one_bit_alu_3 (
    .ALU_Ctrl(ALU_Ctrl), .A(A[2]), .B(B[2]), .C_in(one_bit_alu_2_c_out), .R(R[2]), .C_out(one_bit_alu_3_c_out));
  One_bit_ALU one_bit_alu_4 (
    .ALU_Ctrl(ALU_Ctrl), .A(A[3]), .B(B[3]), .C_in(one_bit_alu_3_c_out), .R(R[3]), .C_out(C_out));
endmodule

module ALU32 (
  input  [3:0] ALU_Ctrl,
  input  [31:0] A,
  input  [31:0] B,
  output [31:0] R,
  output C_out
);

  wire alu4_1_c_out, alu4_2_c_out, alu4_3_c_out, alu4_4_c_out, alu4_5_c_out, alu4_6_c_out, alu4_7_c_out;

  ALU4 alu4_1 (.ALU_Ctrl(ALU_Ctrl), .A(A[3:0]), .B(B[3:0]), .C_in(ALU_Ctrl[2]), .R(R[3:0]), .C_out(alu4_1_c_out));
  ALU4 alu4_2 (.ALU_Ctrl(ALU_Ctrl), .A(A[7:4]), .B(B[7:4]), .C_in(alu4_1_c_out), .R(R[7:4]), .C_out(alu4_2_c_out));
  ALU4 alu4_3 (.ALU_Ctrl(ALU_Ctrl), .A(A[11:8]), .B(B[11:8]), .C_in(alu4_2_c_out), .R(R[11:8]), .C_out(alu4_3_c_out));
  ALU4 alu4_4 (
    .ALU_Ctrl(ALU_Ctrl), .A(A[15:12]), .B(B[15:12]), .C_in(alu4_3_c_out), .R(R[15:12]), .C_out(alu4_4_c_out));
  ALU4 alu4_5 (
    .ALU_Ctrl(ALU_Ctrl), .A(A[19:16]), .B(B[19:16]), .C_in(alu4_4_c_out), .R(R[19:16]), .C_out(alu4_5_c_out));
  ALU4 alu4_6 (
    .ALU_Ctrl(ALU_Ctrl), .A(A[23:20]), .B(B[23:20]), .C_in(alu4_5_c_out), .R(R[23:20]), .C_out(alu4_6_c_out));
  ALU4 alu4_7 (
    .ALU_Ctrl(ALU_Ctrl), .A(A[27:24]), .B(B[27:24]), .C_in(alu4_6_c_out), .R(R[27:24]), .C_out(alu4_7_c_out));
  ALU4 alu4_8 (.ALU_Ctrl(ALU_Ctrl), .A(A[31:28]), .B(B[31:28]), .C_in(alu4_7_c_out), .R(R[31:28]), .C_out(C_out));
endmodule

module Datapath (
  input  [31:0] Instruction
);

  wire clock_1_out, control_1_alu_src;
  wire [3:0] control_1_alu_ctrl0;
  wire [31:0] alu32_1_r, bit_extender_1_out, multiplexer_1_out, reg_file2_1_rdata1, reg_file2_1_rdata2;

  Clock clock_1 (.out(clock_1_out));
  assign bit_extender_1_out = {{20{Instruction[31]}}, Instruction[31:20]};  // Bit_Extender bit_extender_1
  reg_file2 reg_file2_1 (
    .RReg1(Instruction[19:15]), .RReg2(Instruction[24:20]), .WData(alu32_1_r), .Clock_in(clock_1_out),
    .Write(1'b1), .WReg(Instruction[11:7]), .RData1(reg_file2_1_rdata1), .RData2(reg_file2_1_rdata2));
  Multiplexer #(.enable("false"), .width(32)) multiplexer_1 (
    .in0(reg_file2_1_rdata2), .in1(bit_extender_1_out), .out(multiplexer_1_out), .sel(control_1_alu_src));
  Control control_1 (
    .I30(Instruction[30]), .I14(Instruction[14]), .I13(Instruction[13]), .I12(Instruction[12]),
    .I6(Instruction[6]), .I5(Instruction[5]), .I4(Instruction[4]), .ALU_CTRL3(control_1_alu_ctrl0[3]),
    .ALU_CTRL2(control_1_alu_ctrl0[2]), .ALU_CTRL1(control_1_alu_ctrl0[1]),
    .ALU_CTRL0(control_1_alu_ctrl0[0]), .ALU_Src(control_1_alu_src));
  ALU32 alu32_1 (
    .ALU_Ctrl(control_1_alu_ctrl0), .A(reg_file2_1_rdata1), .B(multiplexer_1_out), .R(alu32_1_r));  // open: C_out
endmodule

module reg_file (
  input  [1:0] RReg1,
  input  [1:0] RReg2,
  input  [31:0] WData,
  input  Clock_in,
  input  Write,
  input  [1:0] WReg,
  output [31:0] RData1,
  output [31:0] RData2
);

  wire demultiplexer_1_out0, demultiplexer_1_out1, demultiplexer_1_out2, demultiplexer_1_out3;
  wire [31:0] register_1_q, register_2_q, register_3_q, register_4_q;

  Demultiplexer #(.enable("false"), .select(2)) demultiplexer_1 (
    .out0(demultiplexer_1_out0), .out1(demultiplexer_1_out1), .out2(demultiplexer_1_out2),
    .out3(demultiplexer_1_out3), .in(Write), .sel(WReg));
  Register #(.width(32)) register_1 (
    .D(WData), .en(demultiplexer_1_out0), .clk(Clock_in), .Q(register_1_q), .clr(Write));
  Register #(.width(32)) register_2 (
    .D(WData), .en(demultiplexer_1_out1), .clk(Clock_in), .Q(register_2_q));  // open: clr
  Register #(.width(32)) register_3 (
    .D(WData), .en(demultiplexer_1_out2), .clk(Clock_in), .Q(register_3_q));  // open: clr
  Register #(.width(32)) register_4 (
    .D(WData), .en(demultiplexer_1_out3), .clk(Clock_in), .Q(register_4_q));  // open: clr
  Multiplexer #(.enable("false"), .select(2), .width(32)) multiplexer_1 (
    .in0(register_1_q), .in1(register_2_q), .in2(register_3_q), .in3(register_4_q), .out(RData1), .sel(RReg1));
  Multiplexer #(.enable("false"), .select(2), .width(32)) multiplexer_2 (
    .in0(register_1_q), .in1(register_2_q), .in2(register_3_q), .in3(register_4_q), .out(RData2), .sel(RReg2));
endmodule

module reg_file2 (
  input  [4:0] RReg1,
  input  [4:0] RReg2,
  input  [31:0] WData,
  input  Clock_in,
  input  Write,
  input  [4:0] WReg,
  output [31:0] RData1,
  output [31:0] RData2
);

  wire demultiplexer_1_out0, demultiplexer_1_out1, demultiplexer_1_out2, demultiplexer_1_out3,
       demultiplexer_1_out4, demultiplexer_1_out5, demultiplexer_1_out6, demultiplexer_1_out7,
       demultiplexer_1_out8, demultiplexer_1_out9, demultiplexer_1_out10, demultiplexer_1_out11,
       demultiplexer_1_out12, demultiplexer_1_out13, demultiplexer_1_out14, demultiplexer_1_out15,
       demultiplexer_1_out16, demultiplexer_1_out17, demultiplexer_1_out18, demultiplexer_1_out19,
       demultiplexer_1_out20, demultiplexer_1_out21, demultiplexer_1_out22, demultiplexer_1_out23,
       demultiplexer_1_out24, demultiplexer_1_out25, demultiplexer_1_out26, demultiplexer_1_out27,
       demultiplexer_1_out28, demultiplexer_1_out29, demultiplexer_1_out30, demultiplexer_1_out31;
  wire [31:0] Reg1, Reg2, Reg3, Reg4, Reg5, Reg6, Reg7, Reg8, Reg9, Reg10, Reg11, Reg12, Reg13, Reg14, Reg15,
       Reg16, Reg17, Reg18, Reg19, Reg20, Reg21, Reg22, Reg23, Reg24, Reg25, Reg26, Reg27, Reg28, Reg29,
       Reg30, Reg31, Reg32, register_15_q, register_16_q;

  Demultiplexer #(.enable("false"), .select(5)) demultiplexer_1 (
    .out0(demultiplexer_1_out0), .out1(demultiplexer_1_out1), .out2(demultiplexer_1_out2),
    .out3(demultiplexer_1_out3), .out4(demultiplexer_1_out4), .out5(demultiplexer_1_out5),
    .out6(demultiplexer_1_out6), .out7(demultiplexer_1_out7), .out8(demultiplexer_1_out8),
    .out9(demultiplexer_1_out9), .out10(demultiplexer_1_out10), .out11(demultiplexer_1_out11),
    .out12(demultiplexer_1_out12), .out13(demultiplexer_1_out13), .out14(demultiplexer_1_out14),
    .out15(demultiplexer_1_out15), .out16(demultiplexer_1_out16), .out17(demultiplexer_1_out17),
    .out18(demultiplexer_1_out18), .out19(demultiplexer_1_out19), .out20(demultiplexer_1_out20),
    .out21(demultiplexer_1_out21), .out22(demultiplexer_1_out22), .out23(demultiplexer_1_out23),
    .out24(demultiplexer_1_out24), .out25(demultiplexer_1_out25), .out26(demultiplexer_1_out26),
    .out27(demultiplexer_1_out27), .out28(demultiplexer_1_out28), .out29(demultiplexer_1_out29),
    .out30(demultiplexer_1_out30), .out31(demultiplexer_1_out31), .in(Write), .sel(WReg));
  Register #(.width(32)) register_1 (.D(WData), .en(demultiplexer_1_out0), .clk(Clock_in), .Q(Reg1), .clr(Write));
  Register #(.width(32)) register_2 (.D(WData), .en(demultiplexer_1_out2), .clk(Clock_in), .Q(Reg3));  // open: clr
  Register #(.width(32)) register_3 (.D(WData), .en(demultiplexer_1_out4), .clk(Clock_in), .Q(Reg5));  // open: clr
  Register #(.width(32)) register_4 (.D(WData), .en(demultiplexer_1_out6), .clk(Clock_in), .Q(Reg7));  // open: clr
  Register #(.width(32)) register_5 (.D(WData), .en(demultiplexer_1_out8), .clk(Clock_in), .Q(Reg9));  // open: clr
  Register #(.width(32)) register_6 (.D(WData), .en(demultiplexer_1_out10), .clk(Clock_in), .Q(Reg11));  // open: clr
  Register #(.width(32)) register_7 (.D(WData), .en(demultiplexer_1_out12), .clk(Clock_in), .Q(Reg13));  // open: clr
  Register #(.width(32)) register_8 (.D(WData), .en(demultiplexer_1_out14), .clk(Clock_in), .Q(Reg15));  // open: clr
  Register #(.width(32)) register_9 (.D(WData), .en(demultiplexer_1_out16), .clk(Clock_in), .Q(Reg17));  // open: clr
  Register #(.width(32)) register_10 (.D(WData), .en(demultiplexer_1_out18), .clk(Clock_in), .Q(Reg19));  // open: clr
  Register #(.width(32)) register_11 (.D(WData), .en(demultiplexer_1_out20), .clk(Clock_in), .Q(Reg21));  // open: clr
  Register #(.width(32)) register_12 (.D(WData), .en(demultiplexer_1_out22), .clk(Clock_in), .Q(Reg23));  // open: clr
  Register #(.width(32)) register_13 (.D(WData), .en(demultiplexer_1_out24), .clk(Clock_in), .Q(Reg25));  // open: clr
  Register #(.width(32)) register_14 (.D(WData), .en(demultiplexer_1_out26), .clk(Clock_in), .Q(Reg27));  // open: clr
  Register #(.width(32)) register_15 (
    .D(WData), .en(demultiplexer_1_out28), .clk(Clock_in), .Q(register_15_q));  // open: clr
  Register #(.width(32)) register_16 (
    .D(WData), .en(demultiplexer_1_out30), .clk(Clock_in), .Q(register_16_q));  // open: clr
  Register #(.width(32)) register_17 (.D(WData), .en(demultiplexer_1_out1), .clk(Clock_in), .Q(Reg2));  // open: clr
  Register #(.width(32)) register_18 (.D(WData), .en(demultiplexer_1_out3), .clk(Clock_in), .Q(Reg4));  // open: clr
  Register #(.width(32)) register_19 (.D(WData), .en(demultiplexer_1_out5), .clk(Clock_in), .Q(Reg6));  // open: clr
  Register #(.width(32)) register_20 (.D(WData), .en(demultiplexer_1_out7), .clk(Clock_in), .Q(Reg8));  // open: clr
  Register #(.width(32)) register_21 (.D(WData), .en(demultiplexer_1_out9), .clk(Clock_in), .Q(Reg10));  // open: clr
  Register #(.width(32)) register_22 (.D(WData), .en(demultiplexer_1_out11), .clk(Clock_in), .Q(Reg12));  // open: clr
  Register #(.width(32)) register_23 (.D(WData), .en(demultiplexer_1_out13), .clk(Clock_in), .Q(Reg14));  // open: clr
  Register #(.width(32)) register_24 (.D(WData), .en(demultiplexer_1_out15), .clk(Clock_in), .Q(Reg16));  // open: clr
  Register #(.width(32)) register_25 (.D(WData), .en(demultiplexer_1_out17), .clk(Clock_in), .Q(Reg18));  // open: clr
  Register #(.width(32)) register_26 (.D(WData), .en(demultiplexer_1_out19), .clk(Clock_in), .Q(Reg20));  // open: clr
  Register #(.width(32)) register_27 (.D(WData), .en(demultiplexer_1_out21), .clk(Clock_in), .Q(Reg22));  // open: clr
  Register #(.width(32)) register_28 (.D(WData), .en(demultiplexer_1_out23), .clk(Clock_in), .Q(Reg24));  // open: clr
  Register #(.width(32)) register_29 (.D(WData), .en(demultiplexer_1_out25), .clk(Clock_in), .Q(Reg26));  // open: clr
  Register #(.width(32)) register_30 (.D(WData), .en(demultiplexer_1_out27), .clk(Clock_in));  // open: Q, clr
  Register #(.width(32)) register_31 (.D(WData), .en(demultiplexer_1_out29), .clk(Clock_in));  // open: Q, clr
  Register #(.width(32)) register_32 (.D(WData), .en(demultiplexer_1_out31), .clk(Clock_in));  // open: Q, clr
  Multiplexer #(.enable("false"), .select(5), .width(32)) multiplexer_1 (
    .in0(Reg1), .in1(Reg2), .in2(Reg3), .in3(Reg4), .in4(Reg5), .in5(Reg6), .in6(Reg7), .in7(Reg8),
    .in8(Reg9), .in9(Reg10), .in10(Reg11), .in11(Reg12), .in12(Reg13), .in13(Reg14), .in14(Reg15),
    .in15(Reg16), .in16(Reg17), .in17(Reg18), .in18(Reg19), .in19(Reg20), .in20(Reg21), .in21(Reg22),
    .in22(Reg23), .in23(Reg24), .in24(Reg25), .in25(Reg26), .in26(Reg27), .in27(Reg28), .in28(Reg29),
    .in29(Reg30), .in30(Reg31), .in31(Reg32), .out(RData1), .sel(RReg1));
  Multiplexer #(.enable("false"), .select(5), .width(32)) multiplexer_2 (
    .in0(Reg1), .in1(Reg2), .in2(Reg3), .in3(Reg4), .in4(Reg5), .in5(Reg6), .in6(Reg7), .in7(Reg8),
    .in8(Reg9), .in9(Reg10), .in10(Reg11), .in11(Reg12), .in12(Reg13), .in13(Reg14), .in14(Reg15),
    .in15(Reg16), .in16(Reg17), .in17(Reg18), .in18(Reg19), .in19(Reg20), .in20(Reg21), .in21(Reg22),
    .in22(Reg23), .in23(Reg24), .in24(Reg25), .in25(Reg26), .in26(Reg27), .in27(Reg28), .in28(Reg29),
    .in29(Reg30), .in30(Reg31), .in31(Reg32), .out(RData2), .sel(RReg2));
endmodule
