// Logisim project Lab4.circ as structural Verilog: 11 circuits, main circuit Processor
module InstructionMemory (
  input  [23:0] Address,
  input  ClockIn,
  output [31:0] Instruction
);

  wire not_1_out;

  not not_1 (not_1_out, ClockIn);
  RAM #(.addrWidth(22), .asyncread("true"), .dataWidth(32)) ram_1 (
    .addr(Address[23:2]), .we(1'b0), .oe(not_1_out), .dout(Instruction));  // open: clk, din
endmodule

module Processor (
);

  wire alu_ctrl_1_alu_src, and_1_out, clock_1_out, comparator_1_eq, control_1_branch, control_1_memread,
       control_1_memtoreg, control_1_memwrite, control_1_regwrite;
  wire [3:0] alu_ctrl_1_alu_ctrl0;
  wire [31:0] adder_1_out, adder_2_out, alu32_1_r, datamemory_1_readdata, immgen_1_imm32,
       instructionmemory_1_instruction, multiplexer_1_out, multiplexer_2_out, multiplexer_3_out,
       register_1_q, register_file_1_rdata1, register_file_1_rdata2;

  Register #(.width(32)) register_1 (
    .D(multiplexer_2_out), .en(1'b1), .clk(clock_1_out), .Q(register_1_q));  // open: clr
  Clock clock_1 (.out(clock_1_out));
  Adder #(.width(32)) adder_1 (.a(register_1_q), .b(32'h4), .out(adder_1_out));  // open: cin, cout
  InstructionMemory instructionmemory_1 (
    .Address(register_1_q[23:0]), .ClockIn(clock_1_out), .Instruction(instructionmemory_1_instruction));
  ImmGen immgen_1 (.Instruction(instructionmemory_1_instruction), .IMM32(immgen_1_imm32));
  ALU_Ctrl alu_ctrl_1 (
    .I30(instructionmemory_1_instruction[30]), .I14(instructionmemory_1_instruction[14]),
    .I13(instructionmemory_1_instruction[13]), .I12(instructionmemory_1_instruction[12]),
    .I6(instructionmemory_1_instruction[6]), .I5(instructionmemory_1_instruction[5]),
    .I4(instructionmemory_1_instruction[4]), .ALU_CTRL3(alu_ctrl_1_alu_ctrl0[3]),
    .ALU_CTRL2(alu_ctrl_1_alu_ctrl0[2]), .ALU_CTRL1(alu_ctrl_1_alu_ctrl0[1]),
    .ALU_CTRL0(alu_ctrl_1_alu_ctrl0[0]), .ALU_Src(alu_ctrl_1_alu_src));
  Control control_1 (
    .I6(instructionmemory_1_instruction[6:0]), .MemtoReg(control_1_memtoreg), .RegWrite(control_1_regwrite),
    .MemRead(control_1_memread), .MemWrite(control_1_memwrite), .Branch(control_1_branch));
  Register_File register_file_1 (
    .RReg1(instructionmemory_1_instruction[19:15]), .RReg2(instructionmemory_1_instruction[24:20]),
    .WData(multiplexer_3_out), .Clock_in(clock_1_out), .Write(control_1_regwrite),
    .WReg(instructionmemory_1_instruction[11:7]), .RData1(register_file_1_rdata1),
    .RData2(register_file_1_rdata2));
  Multiplexer #(.enable("false"), .width(32)) multiplexer_1 (
    .in0(register_file_1_rdata2), .in1(immgen_1_imm32), .out(multiplexer_1_out), .sel(alu_ctrl_1_alu_src));
  Adder #(.width(32)) adder_2 (.a(register_1_q), .b(immgen_1_imm32), .out(adder_2_out));  // open: cin, cout
  Comparator #(.width(32)) comparator_1 (
    .a(register_file_1_rdata1), .b(register_file_1_rdata2), .eq(comparator_1_eq));  // open: gt, lt
  and and_1 (and_1_out, control_1_branch, comparator_1_eq);
  ALU32 alu32_1 (
    .ALU_Ctrl(alu_ctrl_1_alu_ctrl0), .A(register_file_1_rdata1), .B(multiplexer_1_out), .R(alu32_1_r));  // open: C_out
  Multiplexer #(.enable("false"), .width(32)) multiplexer_2 (
    .in0(adder_1_out), .in1(adder_2_out), .out(multiplexer_2_out), .sel(and_1_out));
  DataMemory datamemory_1 (
    .Address(alu32_1_r[25:0]), .MemWrite(control_1_memwrite), .MemRead(control_1_memread),
    .ClockIn(clock_1_out), .WriteData(register_file_1_rdata2), .ReadData(datamemory_1_readdata));
  Multiplexer #(.enable("false"), .width(32)) multiplexer_3 (
    .in0(alu32_1_r), .in1(datamemory_1_readdata), .out(multiplexer_3_out), .sel(control_1_memtoreg));
endmodule

module DataMemory (
  input  [25:0] Address,
  input  MemWrite,
  input  MemRead,
  input  ClockIn,
  input  [31:0] WriteData,
  output [31:0] ReadData
);

  RAM #(.addrWidth(24), .asyncread("true"), .dataWidth(32)) ram_1 (
    .addr(Address[25:2]), .we(MemWrite), .oe(MemRead), .clk(ClockIn), .din(WriteData), .dout(ReadData));
endmodule

module Register_File (
  input  [4:0] RReg1,
  input  [4:0] RReg2,
  input  [31:0] WData,
  input  Clock_in,
  input  Write,
  input  [4:0] WReg,
  output [31:0] RData1,
  output [31:0] RData2
);

  wire demultiplexer_1_out0, demultiplexer_1_out1, demultiplexer_1_out2, demultiplexer_1_out3,
       demultiplexer_1_out4, demultiplexer_1_out5, demultiplexer_1_out6, demultiplexer_1_out7,
       demultiplexer_1_out8, demultiplexer_1_out9, demultiplexer_1_out10, demultiplexer_1_out11,
       demultiplexer_1_out12, demultiplexer_1_out13, demultiplexer_1_out14, demultiplexer_1_out15,
       demultiplexer_1_out16, demultiplexer_1_out17, demultiplexer_1_out18, demultiplexer_1_out19,
       demultiplexer_1_out20, demultiplexer_1_out21, demultiplexer_1_out22, demultiplexer_1_out23,
       demultiplexer_1_out24, demultiplexer_1_out25, demultiplexer_1_out26, demultiplexer_1_out27,
       demultiplexer_1_out28, demultiplexer_1_out29, demultiplexer_1_out30, demultiplexer_1_out31;
  wire [31:0] Reg0, Reg1, Reg2, Reg3, Reg4, Reg5, Reg6, Reg7, Reg8, Reg9, Reg10, Reg11, Reg12, Reg13, Reg14,
       Reg15, Reg16, Reg17, Reg18, Reg19, Reg20, Reg21, Reg22, Reg23, Reg24, Reg25, Reg26, Reg27, Reg28,
       Reg29, Reg30, Reg31, undriven;

  Demultiplexer #(.enable("false"), .select(5)) demultiplexer_1 (
    .out0(demultiplexer_1_out0), .out1(demultiplexer_1_out1), .out2(demultiplexer_1_out2),
    .out3(demultiplexer_1_out3), .out4(demultiplexer_1_out4), .out5(demultiplexer_1_out5),
    .out6(demultiplexer_1_out6), .out7(demultiplexer_1_out7), .out8(demultiplexer_1_out8),
    .out9(demultiplexer_1_out9), .out10(demultiplexer_1_out10), .out11(demultiplexer_1_out11),
    .out12(demultiplexer_1_out12), .out13(demultiplexer_1_out13), .out14(demultiplexer_1_out14),
    .out15(demultiplexer_1_out15), .out16(demultiplexer_1_out16), .out17(demultiplexer_1_out17),
    .out18(demultiplexer_1_out18), .out19(demultiplexer_1_out19), .out20(demultiplexer_1_out20),
    .out21(demultiplexer_1_out21), .out22(demultiplexer_1_out22), .out23(demultiplexer_1_out23),
    .out24(demultiplexer_1_out24), .out25(demultiplexer_1_out25), .out26(demultiplexer_1_out26),
    .out27(demultiplexer_1_out27), .out28(demultiplexer_1_out28), .out29(demultiplexer_1_out29),
    .out30(demultiplexer_1_out30), .out31(demultiplexer_1_out31), .in(Write), .sel(WReg));
  Register #(.width(32)) register_1 (.D(WData), .en(demultiplexer_1_out0), .clk(Clock_in), .Q(Reg0), .clr(Write));
  Register #(.width(32)) register_2 (.D(WData), .en(demultiplexer_1_out2), .clk(Clock_in), .Q(Reg2));  // open: clr
  Register #(.width(32)) register_3 (.D(WData), .en(demultiplexer_1_out4), .clk(Clock_in), .Q(Reg4));  // open: clr
  Register #(.width(32)) register_4 (.D(WData), .en(demultiplexer_1_out6), .clk(Clock_in), .Q(Reg6));  // open: clr
  Register #(.width(32)) register_5 (.D(WData), .en(demultiplexer_1_out8), .clk(Clock_in), .Q(Reg8));  // open: clr
  Register #(.width(32)) register_6 (.D(WData), .en(demultiplexer_1_out10), .clk(Clock_in), .Q(Reg10));  // open: clr
  Register #(.width(32)) register_7 (.D(WData), .en(demultiplexer_1_out12), .clk(Clock_in), .Q(Reg12));  // open: clr
  Register #(.width(32)) register_8 (.D(WData), .en(demultiplexer_1_out14), .clk(Clock_in), .Q(Reg14));  // open: clr
  Register #(.width(32)) register_9 (.D(WData), .en(demultiplexer_1_out16), .clk(Clock_in), .Q(Reg16));  // open: clr
  Register #(.width(32)) register_10 (.D(WData), .en(demultiplexer_1_out18), .clk(Clock_in), .Q(Reg18));  // open: clr
  Register #(.width(32)) register_11 (.D(WData), .en(demultiplexer_1_out20), .clk(Clock_in), .Q(Reg20));  // open: clr
  Register #(.width(32)) register_12 (.D(WData), .en(demultiplexer_1_out22), .clk(Clock_in), .Q(Reg22));  // open: clr
  Register #(.width(32)) register_13 (.D(WData), .en(demultiplexer_1_out24), .clk(Clock_in), .Q(Reg24));  // open: clr
  Register #(.width(32)) register_14 (.D(WData), .en(demultiplexer_1_out26), .clk(Clock_in), .Q(Reg26));  // open: clr
  Register #(.width(32)) register_15 (.D(WData), .en(demultiplexer_1_out28), .clk(Clock_in), .Q(Reg28));  // open: clr
  Register #(.width(32)) register_16 (.D(WData), .en(demultiplexer_1_out30), .clk(Clock_in), .Q(Reg30));  // open: clr
  Register #(.width(32)) register_17 (.D(WData), .en(demultiplexer_1_out1), .clk(Clock_in), .Q(Reg1));  // open: clr
  Register #(.width(32)) register_18 (.D(WData), .en(demultiplexer_1_out3), .clk(Clock_in), .Q(Reg3));  // open: clr
  Register #(.width(32)) register_19 (.D(WData), .en(demultiplexer_1_out5), .clk(Clock_in), .Q(Reg5));  // open: clr
  Register #(.width(32)) register_20 (.D(WData), .en(demultiplexer_1_out7), .clk(Clock_in), .Q(Reg7));  // open: clr
  Register #(.width(32)) register_21 (.D(WData), .en(demultiplexer_1_out9), .clk(Clock_in), .Q(Reg9));  // open: clr
  Register #(.width(32)) register_22 (.D(WData), .en(demultiplexer_1_out11), .clk(Clock_in), .Q(Reg11));  // open: clr
  Register #(.width(32)) register_23 (.D(WData), .en(demultiplexer_1_out13), .clk(Clock_in), .Q(Reg13));  // open: clr
  Register #(.width(32)) register_24 (.D(WData), .en(demultiplexer_1_out15), .clk(Clock_in), .Q(Reg15));  // open: clr
  Register #(.width(32)) register_25 (.D(WData), .en(demultiplexer_1_out17), .clk(Clock_in), .Q(Reg17));  // open: clr
  Register #(.width(32)) register_26 (.D(WData), .en(demultiplexer_1_out19), .clk(Clock_in), .Q(Reg19));  // open: clr
  Register #(.width(32)) register_27 (.D(WData), .en(demultiplexer_1_out21), .clk(Clock_in), .Q(Reg21));  // open: clr
  Register #(.width(32)) register_28 (.D(WData), .en(demultiplexer_1_out23), .clk(Clock_in), .Q(Reg23));  // open: clr
  Register #(.width(32)) register_29 (.D(WData), .en(demultiplexer_1_out25), .clk(Clock_in), .Q(Reg25));  // open: clr
  Register #(.width(32)) register_30 (.D(WData), .en(demultiplexer_1_out27), .clk(Clock_in), .Q(Reg27));  // open: clr
  Register #(.width(32)) register_31 (.D(WData), .en(demultiplexer_1_out29), .clk(Clock_in), .Q(Reg29));  // open: clr
  Register #(.width(32)) register_32 (.D(WData), .en(demultiplexer_1_out31), .clk(Clock_in), .Q(Reg31));  // open: clr
  Multiplexer #(.enable("false"), .select(5), .width(32)) multiplexer_1 (
    .in0(Reg0), .in1(Reg1), .in2(Reg2), .in3(Reg3), .in4(Reg4), .in5(Reg5), .in6(Reg6), .in7(Reg7),
    .in8(Reg8), .in9(Reg9), .in10(Reg10), .in11(Reg11), .in12(Reg12), .in13(Reg13), .in14(Reg14),
    .in15(Reg15), .in16(Reg16), .in17(Reg17), .in18(Reg18), .in19(Reg19), .in20(Reg20), .in21(Reg21),
    .in22(Reg22), .in23(Reg23), .in24(Reg24), .in25(Reg25), .in26(Reg26), .in27(Reg27), .in28(Reg28),
    .in29(Reg29), .in30(Reg30), .in31(Reg31), .out(RData1), .sel(RReg1));
  Multiplexer #(.enable("false"), .select(5), .width(32)) multiplexer_2 (
    .in0(Reg0), .in1(Reg1), .in2(Reg2), .in3(Reg3), .in4(Reg4), .in5(Reg5), .in6(Reg6), .in7(Reg7),
    .in8(Reg8), .in9(undriven), .in10(Reg10), .in11(Reg11), .in12(Reg12), .in13(Reg13), .in14(Reg14),
    .in15(Reg15), .in16(Reg16), .in17(Reg17), .in18(Reg18), .in19(Reg19), .in20(Reg20), .in21(Reg21),
    .in22(Reg22), .in23(Reg23), .in24(Reg24), .in25(Reg25), .in26(Reg26), .in27(Reg27), .in28(Reg28),
    .in29(Reg29), .in30(Reg30), .in31(Reg31), .out(RData2), .sel(RReg2));
endmodule

module ALU32 (
  input  [3:0] ALU_Ctrl,
  input  [31:0] A,
  input  [31:0] B,
  output [31:0] R,
  output C_out
);

  wire alu4_1_c_out, alu4_2_c_out, alu4_3_c_out, alu4_4_c_out, alu4_5_c_out, alu4_6_c_out, alu4_7_c_out;

  ALU4 alu4_1 (.ALU_Ctrl(ALU_Ctrl), .A(A[3:0]), .B(B[3:0]), .C_in(ALU_Ctrl[2]), .R(R[3:0]), .C_out(alu4_1_c_out));
  ALU4 alu4_2 (.ALU_Ctrl(ALU_Ctrl), .A(A[7:4]), .B(B[7:4]), .C_in(alu4_1_c_out), .R(R[7:4]), .C_out(alu4_2_c_out));
  ALU4 alu4_3 (.ALU_Ctrl(ALU_Ctrl), .A(A[11:8]), .B(B[11:8]), .C_in(alu4_2_c_out), .R(R[11:8]), .C_out(alu4_3_c_out));
  ALU4 alu4_4 (
    .ALU_Ctrl(ALU_Ctrl), .A(A[15:12]), .B(B[15:12]), .C_in(alu4_3_c_out), .R(R[15:12]), .C_out(alu4_4_c_out));
  ALU4 alu4_5 (
    .ALU_Ctrl(ALU_Ctrl), .A(A[19:16]), .B(B[19:16]), .C_in(alu4_4_c_out), .R(R[19:16]), .C_out(alu4_5_c_out));
  ALU4 alu4_6 (
    .ALU_Ctrl(ALU_Ctrl), .A(A[23:20]), .B(B[23:20]), .C_in(alu4_5_c_out), .R(R[23:20]), .C_out(alu4_6_c_out));
  ALU4 alu4_7 (
    .ALU_Ctrl(ALU_Ctrl), .A(A[27:24]), .B(B[27:24]), .C_in(alu4_6_c_out), .R(R[27:24]), .C_out(alu4_7_c_out));
  ALU4 alu4_8 (.ALU_Ctrl(ALU_Ctrl), .A(A[31:28]), .B(B[31:28]), .C_in(alu4_7_c_out), .R(R[31:28]), .C_out(C_out));
endmodule

module ALU4 (
  input  [3:0] ALU_Ctrl,
  input  [3:0] A,
  input  [3:0] B,
  input  C_in,
  output [3:0] R,
  output C_out
);

  wire alu1_1_c_out, alu1_2_c_out, alu1_3_c_out;

  ALU1 alu1_1 (.ALU_Ctrl(ALU_Ctrl), .A(A[0]), .B(B[0]), .C_in(C_in), .R(R[0]), .C_out(alu1_1_c_out));
  ALU1 alu1_2 (.ALU_Ctrl(ALU_Ctrl), .A(A[1]), .B(B[1]), .C_in(alu1_1_c_out), .R(R[1]), .C_out(alu1_2_c_out));
  ALU1 alu1_3 (.ALU_Ctrl(ALU_Ctrl), .A(A[2]), .B(B[2]), .C_in(alu1_2_c_out), .R(R[2]), .C_out(alu1_3_c_out));
  ALU1 alu1_4 (.ALU_Ctrl(ALU_Ctrl), .A(A[3]), .B(B[3]), .C_in(alu1_3_c_out), .R(R[3]), .C_out(C_out));
endmodule

module ALU1 (
  input  [3:0] ALU_Ctrl,
  input  A,
  input  B,
  input  C_in,
  output R,
  output C_out
);

  wire add_1_s, and_1_out, multiplexer_1_out, not_1_out, or_1_out, xor_1_out;

  Multiplexer #(.enable("false")) multiplexer_1 (.in0(B), .in1(not_1_out), .out(multiplexer_1_out), .sel(ALU_Ctrl[2]));
  not not_1 (not_1_out, B);
  and and_1 (and_1_out, A, multiplexer_1_out);
  or or_1 (or_1_out, A, multiplexer_1_out);
  xor xor_1 (xor_1_out, A, multiplexer_1_out);
  Multiplexer #(.enable("false"), .select(2)) multiplexer_2 (
    .in0(and_1_out), .in1(or_1_out), .in2(xor_1_out), .in3(add_1_s), .out(R), .sel(ALU_Ctrl[1:0]));
  Add add_1 (.A(A), .B(multiplexer_1_out), .C_in(C_in), .S(add_1_s), .C_out(C_out));
endmodule

module Add (
  input  A,
  input  B,
  input  C_in,
  output S,
  output C_out
);

  wire and_1_out, and_2_out, xor_1_out;

  xor xor_1 (xor_1_out, A, B);
  xor xor_2 (S, xor_1_out, C_in);
  and and_1 (and_1_out, xor_1_out, C_in);
  and and_2 (and_2_out, A, B);
  or or_1 (C_out, and_1_out, and_2_out);
endmodule

module ALU_Ctrl (
  input  I30,
  input  I14,
  input  I13,
  input  I12,
  input  I6,
  input  I5,
  input  I4,
  output ALU_CTRL3,
  output ALU_CTRL2,
  output ALU_CTRL1,
  output ALU_CTRL0,
  output ALU_Src
);

  wire and_2_out, and_3_out, not_1_out, not_2_out, not_3_out, not_4_out, not_5_out;

  not not_1 (not_1_out, I14);
  not not_2 (not_2_out, I13);
  not not_3 (not_3_out, I12);
  not not_4 (not_4_out, I5);
  not not_5 (not_5_out, I4);
  and and_1 (ALU_CTRL2, I30, not_2_out, I5);
  and and_2 (and_2_out, not_1_out, not_4_out);
  and and_3 (and_3_out, I13, not_3_out);
  or or_1 (ALU_Src, not_4_out, not_5_out);
  or or_2 (ALU_CTRL1, and_2_out, not_2_out);
  or or_3 (ALU_CTRL0, not_1_out, and_3_out);

  assign ALU_CTRL3 = 1'b0;
endmodule

module ImmGen (
  input  [31:0] Instruction,
  output [31:0] IMM32
);

  assign IMM32[31:12] = {{19{Instruction[31]}}, Instruction[31]};  // Bit_Extender bit_extender_1
  Multiplexer #(.enable("false"), .width(4)) multiplexer_1 (
    .in0(Instruction[24:21]), .in1(Instruction[11:8]), .out(IMM32[4:1]), .sel(Instruction[5]));
  Multiplexer #(.enable("false")) multiplexer_2 (
    .in0(Instruction[7]), .in1(Instruction[31]), .out(IMM32[11]), .sel(Instruction[6]));
  Multiplexer #(.enable("false"), .select(2)) multiplexer_3 (
    .in0(Instruction[20]), .in1(Instruction[7]), .in3(1'b0), .out(IMM32[0]), .sel(Instruction[6:5]));  // open: in2

  assign IMM32[10:5] = Instruction[30:25];

  // Other names for the same wires on the sheet: I30_I25[5:0] = Instruction[30:25]; I5 = Instruction[5];
  //   I6_I5[1:0] = Instruction[6:5]; I6 = Instruction[6]; I7 = Instruction[7]; I11_I8[3:0] = Instruction[11:8];
  //   I20 = Instruction[20]; I24_I21[3:0] = Instruction[24:21]; I31 = Instruction[31]
endmodule

module Control (
  input  [6:0] I6,
  output MemtoReg,
  output RegWrite,
  output MemRead,
  output MemWrite,
  output Branch
);

  wire not_1_out, not_2_out;

  not not_1 (not_1_out, I6[6]);
  not not_2 (not_2_out, I6[5]);
  not not_3 (MemtoReg, I6[4]);
  or or_1 (RegWrite, not_2_out, I6[4]);
  and and_1 (MemRead, not_2_out, MemtoReg);
  and and_2 (MemWrite, not_1_out, I6[5], MemtoReg);

  assign Branch = I6[6];
endmodule
